# Fritzing sketch circuit (saved by Fritzing 0.9.9b)

parts:
  DFRobot_DFPlayer_Mini1 = DFRobot DFPlayer Mini [part_number=DFR0299]
  R2 = Resistor [tolerance=±5% power=0.25 resistance=1k package=THT]
  J1 = Piezo Speaker
  DC/DC_5v1 = DC/DC 5v [package=DIP]
  パーツ2 = InvenSense MPU6050
  パーツ1 = Arduino Pro Micro (Clone)
  S1 = Toggle Switch [package=THT]
  VCC1 = Battery
  R3 = Resistor [tolerance=±5% power=0.25 resistance=1k package=THT]

nets:
  VCC: DFRobot_DFPlayer_Mini1.VCC, DC/DC_5v1.Vbat, パーツ2.VCC, パーツ1.VCC
  N1: DFRobot_DFPlayer_Mini1.RX, R3.Pin_1
  N2: DFRobot_DFPlayer_Mini1.TX, R2.Pin_1
  N3: DFRobot_DFPlayer_Mini1.SPK_1, J1.pin2
  GND: DFRobot_DFPlayer_Mini1.GND-1, DFRobot_DFPlayer_Mini1.GND-2, DC/DC_5v1.Vout, パーツ2.GND, パーツ1.GND, VCC1.-
  N4: DFRobot_DFPlayer_Mini1.SPK_2, J1.pin1
  N5: R2.Pin_0, パーツ1.A2
  N6: DC/DC_5v1.lx, S1.COM
  N7: パーツ2.SCL, パーツ1.D3
  N8: パーツ2.SDA, パーツ1.D2
  N9: パーツ1.A3, R3.Pin_0
  N10: S1.L1, VCC1.+

custom parts:
  DC/DC 5v: DC to 5v DC converter.
